# Fritzing sketch Project sketch (saved by Fritzing 0.9.10b)
breadboards: 1

parts:
  LCM1602_IIC1 = LCM1602 IIC [part_number="LCM1602 IIC" chip_label="LCM1602 IIC" package="DIP (Dual Inline) [THT]"]
  LCD1 = LCD screen
  Onderdeel1 = RFID-RC522-v2
  Onderdeel2 = Arduino Uno (Rev3) - ICSP
  Onderdeel3 = I2C level shifter bidirectional
  WeMos_D1_Mini1 = WeMos D1 Mini  # not connected
  HC-SR04_Sensor_1 = HC-SR04 Ultrasonic Distance Sensor
  SM1 = 28BYJ-48 Stepper Motor [part_number=28BYJ-48]
  Driver1 = 28BYJ-48 Driver Module [part_number=ULN2003 package=THT]

nets:
  VSS: LCM1602_IIC1.VSS, LCD1.VSS
  VDD: LCM1602_IIC1.VDD, LCD1.VDD
  N1: LCM1602_IIC1.V0, LCD1.V0
  N2: LCM1602_IIC1.RS, LCD1.RS
  N3: LCM1602_IIC1.RW, LCD1.R/W
  N4: LCM1602_IIC1.E, LCD1.E
  N5: LCM1602_IIC1.D0, LCD1.DB0
  N6: LCM1602_IIC1.D1, LCD1.DB1
  N7: LCM1602_IIC1.D2, LCD1.DB2
  N8: LCM1602_IIC1.D3, LCD1.DB3
  N9: LCM1602_IIC1.D4, LCD1.DB4
  N10: LCM1602_IIC1.D5, LCD1.DB5
  N11: LCM1602_IIC1.D6, LCD1.DB6
  N12: LCM1602_IIC1.D7, LCD1.DB7
  N13: LCM1602_IIC1.A, LCD1.LED+
  N14: LCM1602_IIC1.K, LCD1.LED-
  GND: LCM1602_IIC1.GND, Onderdeel1.GND, Onderdeel2.GND, Onderdeel3.GND, HC-SR04_Sensor_1.GND
  VCC: LCM1602_IIC1.VCC, Onderdeel2.5V, Onderdeel3.HV, HC-SR04_Sensor_1.VCC
  N15: LCM1602_IIC1.SDA, Onderdeel2.A4/SDA
  N16: LCM1602_IIC1.SCL, Onderdeel2.A5/SCL
  N17: Onderdeel1.SCK, Onderdeel2.D10_PWM/SS
  N18: Onderdeel1.MOSI, Onderdeel2.D13/SCK
  N19: Onderdeel1.MISO, Onderdeel2.D11_PWM/MOSI
  N20: Onderdeel1.IRQ, Onderdeel2.D12/MISO
  N21: Onderdeel1.RST, Onderdeel2.D9_PWM
  N22: Onderdeel1.3_3V, Onderdeel2.3V3
  N23: Onderdeel2.D0/RX, Onderdeel3.HV1
  N24: Onderdeel2.D1/TX, Onderdeel3.HV2
  N25: Onderdeel2.D2, Driver1.IN4
  N26: Onderdeel2.D3_PWM, Driver1.IN3
  N27: Onderdeel2.D4, Driver1.IN2
  N28: Onderdeel2.D5_PWM, Driver1.IN1
  N29: Onderdeel2.D6_PWM, HC-SR04_Sensor_1.ECHO
  N30: Onderdeel2.D7, HC-SR04_Sensor_1.TRIG
  N31: SM1.blue-pin, Driver1.blue-pin
  N32: SM1.pink-pin, Driver1.pink-pin
  N33: SM1.yellow-pin, Driver1.yellow-pin
  N34: SM1.orange-pin, Driver1.orange-pin
  N35: SM1.red-pin, Driver1.red-pin

custom parts:
  LCM1602 IIC: I2C-Module to use a 1602 or 2004 LCD on with the wire.h libory Serial LCD Modul
  RFID-RC522-v2: A simple China made RFID-RC522 Reader; do check the pin labels, as this is a MFRC522 based clone.
  28BYJ-48 Stepper Motor: Unipolar Stepper Motor 28BYJ-48 Top coil - pink & orange Bottom coil - blue & yellow Common rail - red Connector pins: blue - pink - yellow - orange - red
  28BYJ-48 Driver Module: Generic male header
